// Logisim project R8_uC_portIO_diagram.circ as structural Verilog: 1 circuit, main circuit port_io
module port_io (
  input  clk,
  input  rst,
  input  data_in,
  input  [1:0] address,
  output data_out
);

  wire and_1_out, and_2_out, controlled_buffer_1_out, controlled_buffer_2_out, decoder_1_out0,
       decoder_1_out1, decoder_1_out2, multiplexer_1_out, or_1_out, PortConfig_q, PortData_q, PortEnable_q,
       synch_q;

  Decoder #(.select(2)) decoder_1 (
    .out0(decoder_1_out0), .out1(decoder_1_out1), .out2(decoder_1_out2), .sel(address));  // open: out3, en
  Multiplexer #(.enable("false")) multiplexer_1 (
    .in0(synch_q), .in1(data_in), .out(multiplexer_1_out), .sel(and_1_out));
  or or_1 (or_1_out, decoder_1_out2, PortConfig_q);
  Register #(.width(1)) PortConfig (.D(data_in), .en(decoder_1_out1), .Q(PortConfig_q), .clk(clk), .clr(rst));
  Register #(.width(1)) PortEnable (.D(data_in), .en(decoder_1_out0), .Q(PortEnable_q), .clk(clk), .clr(rst));
  Multiplexer #(.select(2), .enable("false")) multiplexer_2 (
    .in0(PortEnable_q), .in1(PortConfig_q), .in2(PortData_q), .out(data_out), .sel(address));  // open: in3
  Register #(.width(1)) PortData (.D(multiplexer_1_out), .en(or_1_out), .Q(PortData_q), .clk(clk), .clr(rst));
  assign controlled_buffer_1_out = and_1_out ? PortData_q : 1'bz;  // Controlled_Buffer controlled_buffer_1
  and and_1 (and_1_out, ~PortConfig_q, PortEnable_q);  // AND_Gate
  and and_2 (and_2_out, PortConfig_q, PortEnable_q);
  assign controlled_buffer_2_out = and_2_out ? controlled_buffer_1_out : 1'bz;  // Controlled_Buffer controlled_buffer_2
  Register #(.width(1)) synch (.D(controlled_buffer_2_out), .en(1'b1), .Q(synch_q));  // open: clk, clr

  // Notes on the sheet:
  //   port_io
endmodule
